# Fritzing sketch rfid-door (saved by Fritzing 0.9.3b)

parts:
  U1 = ESP8266 NodeMCU LoLin module
  WeMos_D1_Mini1 = WeMos D1 Mini
  Matrix_keypad1 = KEYPAD 4x4
  A1 = BBAA100043
  A2 = 2-Channel 5v Relay Shield [package=relay-2ch5v10a]
  U2 = RFID RC522 SIP - 8 pins [chip_label="RFID RC522" package="SIP (Single Inline) [THT]"]
  J1 = Piezo Speaker
  J2 = Power Jack [package=power_jack_slot]
  M1 = DC Motor
  JACK1 = 2.1mm Barrel Jack with Terminal Block  # not connected
  U3 = LM2596 step down module

nets:
  N1: U1.D0, J1.pin2
  N2: U1.D1, U2.RST
  N3: U1.D2, A1.pin1
  N4: U1.D3, A1.pin2
  N5: U1.D4, U2.NSS
  N6: U1.D8, A1.pin3
  N7: U1.RX, WeMos_D1_Mini1.TX
  N8: U1.TX, WeMos_D1_Mini1.RX
  GND: U1.GND, WeMos_D1_Mini1.G, A1.pin4, A2.Pin_10, U2.GND, J1.pin1, J2.GND, M1.pin_2, U3.IN-, U3.OUT-
  N9: U1.Vin, A2.Pin_13, U3.OUT+
  N10: U1.S0, U2.MISO
  N11: U1.SC, U2.SCK
  N12: U1.S1, U2.MOSI
  N13: WeMos_D1_Mini1.D0, Matrix_keypad1.row1
  N14: WeMos_D1_Mini1.D1, Matrix_keypad1.col1
  N15: WeMos_D1_Mini1.D2, Matrix_keypad1.col2
  N16: WeMos_D1_Mini1.D3, Matrix_keypad1.col3
  N17: WeMos_D1_Mini1.D4, Matrix_keypad1.col4
  N18: WeMos_D1_Mini1.D5, Matrix_keypad1.row2
  N19: WeMos_D1_Mini1.D6, Matrix_keypad1.row3
  N20: WeMos_D1_Mini1.D7, Matrix_keypad1.row4
  N21: WeMos_D1_Mini1.D8, A2.Pin_11
  N22: A2.Pin_5, J2.PWR, U3.IN+

notes:
  12v
  5v

custom parts:
  ESP8266 NodeMCU LoLin module: ESP8266 based NodeMCU
  WeMos D1 Mini: The D1 mini is a mini wifi board based on ESP-8266EX.
  KEYPAD 4x4: Matrix keypad 16 buttons, 4 rows x 4 columns
  BBAA100043: BBAA100043 traffic light module.
  2-Channel 5v Relay Shield: 2 Channel 5v Relay Shield w. 2x SPD-06VDC-SD-C
  RFID RC522 SIP - 8 pins: A SIP stand-in part for RFID RC522 . With 8 pins on a 300 mil single inline package (SIP) footprint.
  LM2596 step down module: LM2596 DC-DC step down power supply module 3 A.
